# Fritzing sketch schematic (saved by Fritzing 1.0.7)

parts:
  A1 = Raspberry Pi 5
  J1 = Basic Servo
  Power_plug1 = Power plug
  Buck_Convertor1 = Buck Convertor [part_number=LM2596 package=THT]
  DRV_1 = DRV 8825 Stepper Motor Carrier, High Current [part_number="DRV 8825"]
  C2 = Electrolytic Capacitor [capacitance=100µF voltage=12V package="100 mil [THT, electrolytic]"]
  M1 = Stepper Motor - Bipolar
  A2 = RGB Strip LED

nets:
  5V: A1.5V, J1.vcc, Buck_Convertor1.Positive_Output, DRV_1.VOLTAGE_DD
  GND: A1.GND, J1.gnd, Buck_Convertor1.Negative_Output, DRV_1.GROUND_LOG
  N1: A1.GPIO23, DRV_1.STEP
  N2: A1.GPIO24, DRV_1.DIRECTION
  N3: A1.GPIO25, J1.pulse
  N4: Power_plug1.GND, Buck_Convertor1.Negative_Input, DRV_1.GROUND_ST/_MT, C2.-, A2.Green_Connect, A2.Blue_Connect, A2.Red_Connect
  N5: Power_plug1.VCC, Buck_Convertor1.Positive_Input, DRV_1.VOLTAGE_ST/_MT, C2.+, A2.Common_Connect
  N6: DRV_1.RESET, DRV_1.SLEEP
  N7: DRV_1.OUT_2B, M1.A
  N8: DRV_1.OUT_2A, M1.C
  N9: DRV_1.OUT_1A, M1.B
  N10: DRV_1.OUT_1B, M1.D

notes:
  USB connection to camera module

custom parts:
  Raspberry Pi 5: The RPi5, a faster version of the awesome Raspberry Pi4B ARM Board with 40 pin gpio.
  Buck Convertor: DC to DC buck convertor
  RGB Strip LED: A tri-color Strip LED with red, green and blue. Pin order: red - common cathode - blue - green
